# Fritzing sketch DallasTempWemos2 (saved by Fritzing 0.9.3b)
circuit board: 5cm x 4cm
breadboards: 1

parts:
  DS1 = DS18B20 1-Wire Temperature Sensor [part_number=DS18B20]
  R1 = Resistor [tolerance=±5% resistance=220 package=THT]
  Part1 = NRF24L01+ Breakout Board
  WeMos_D1_Mini = WeMos D1 Mini
  U1 = mystery part, 6 pins [chip_label=BMP280]
  Q1 = HT7333 [part_number=HT7333 package=sot89]
  C2 = Electrolytic Capacitor [capacitance=10µF part_number=C2 voltage=16V package="100 mil [THT, electrolytic]"]
  C1 = Electrolytic Capacitor [capacitance=10µF part_number=C1 voltage=16V package="100 mil [THT, electrolytic]"]
  Batt = Battery
  R2 = Resistor [tolerance=±5% resistance=100k package=THT]
  R3 = Resistor [tolerance=±5% resistance=220k package=THT]

nets:
  GND: DS1.GND, Part1.GND, WeMos_D1_Mini.G, U1.pin2, Q1.GND, C2.-, C1.-, Batt.-, R2.Pin_0
  N1: DS1.DQ, R1.Pin_0, WeMos_D1_Mini.D3
  VDD: DS1.VDD, R1.Pin_1, Part1.VCC, WeMos_D1_Mini.3V3, U1.pin1, U1.pin5, U1.pin6, Q1.Vout, C2.+
  N2: Part1.CE, WeMos_D1_Mini.D4
  N3: Part1.CS, WeMos_D1_Mini.D8
  N4: Part1.SCK, WeMos_D1_Mini.D5
  N5: Part1.MOSI, WeMos_D1_Mini.D7
  N6: Part1.MISO, WeMos_D1_Mini.D6
  N7: WeMos_D1_Mini.A0, R2.Pin_1, R3.Pin_0
  N8: WeMos_D1_Mini.D1, U1.pin3
  N9: WeMos_D1_Mini.D2, U1.pin4
  N10: Q1.Vin, C1.+, Batt.+, R3.Pin_1

notes:
  Temp Sensor v1.0

custom parts:
  HT7333: 3v3 regulator
