# Fritzing sketch RfmMqttGateway (saved by Fritzing 0.9.3b)
circuit board: 6cm x 3cm
breadboards: 1

parts:
  RFM1 = RFM69HCW ISM Transciever
  WeMos_D1_Mini1 = WeMos D1 Mini

nets:
  N1: RFM1.1_GND, WeMos_D1_Mini1.G
  N2: RFM1.4_SCK, WeMos_D1_Mini1.D5
  N3: RFM1.5_MISO, WeMos_D1_Mini1.D6
  N4: RFM1.6_MOSI, WeMos_D1_Mini1.D7
  N5: RFM1.7_NSS, WeMos_D1_Mini1.D8
  N6: RFM1.12_DIO2, WeMos_D1_Mini1.D1
  N7: RFM1.16_3.3V, WeMos_D1_Mini1.3V3

custom parts:
  RFM69HCW ISM Transciever: RF Transceiver by Hope RF. Well supported Arduino libraries are available. This ISM band transceiver is available in several frequencies e.g. 433MHz and 915MHz and it is also available in various feature versions.
